// Logisim project control-logic.circ as structural Verilog: 1 circuit, main circuit control_logic
module control_logic (
  input  [31:0] Instruction,
  input  BrEq,
  input  BrLt,
  output PCSel,
  output RegWEn,
  output [2:0] ImmSel,
  output BrUn,
  output ASel,
  output BSel,
  output [3:0] ALUSel,
  output MemWEn,
  output [1:0] WBSel
);

  wire comparator_1_eq, comparator_2_eq, comparator_3_eq, comparator_4_eq, comparator_5_eq, comparator_6_eq,
       comparator_7_eq, comparator_8_eq, comparator_9_eq, comparator_10_eq;
  wire [2:0] multiplexer_9_out;
  wire [3:0] PriOut;
  wire [5:0] BType, I2Type, I3Type, IType, JType, multiplexer_1_out, multiplexer_2_out, multiplexer_3_out,
       multiplexer_4_out, ROMInput, RType, SType, U2Type, undriven, UType;
  wire [15:14] rom_1_data;

  Multiplexer #(.width(6)) multiplexer_1 (
    .in0(6'b010011), .in1(6'b010100), .out(multiplexer_1_out), .sel(Instruction[30]));
  Multiplexer #(.select(2), .width(6)) multiplexer_2 (
    .in0({6{1'b0}}), .in1(6'b000001), .in2(6'b000010), .out(multiplexer_2_out),
    .sel({Instruction[30], Instruction[25]}));  // open: in3
  Multiplexer #(.select(2), .width(6)) multiplexer_3 (
    .in0(6'b000011), .in1(6'b000100), .out(multiplexer_3_out), .sel({Instruction[30], Instruction[25]}));  // open: in2, in3
  Multiplexer #(.select(2), .width(6)) multiplexer_4 (
    .in0(6'b001000), .in2(6'b001001), .out(multiplexer_4_out), .sel({Instruction[30], Instruction[25]}));  // open: in1, in3
  ROM #(.addrWidth(6), .dataWidth(16)) rom_1 (
    .addr(ROMInput), .data({rom_1_data, WBSel, MemWEn, ALUSel, BSel, ASel, BrUn, ImmSel, RegWEn}));
  Multiplexer #(.select(3), .width(6)) multiplexer_5 (
    .in0(6'b001111), .in1(6'b010000), .in2(6'b010001), .in4(6'b010010), .in5(multiplexer_1_out),
    .in6(6'b010101), .in7(6'b010110), .out(IType), .sel(Instruction[14:12]));  // open: in3
  Comparator #(.width(7)) comparator_1 (.a(Instruction[6:0]), .b(7'b0010011), .eq(comparator_1_eq));  // open: gt, lt
  Comparator #(.width(7)) comparator_2 (.a(Instruction[6:0]), .b(7'b0110011), .eq(comparator_2_eq));  // open: gt, lt
  Comparator #(.width(7)) comparator_3 (.a(Instruction[6:0]), .b(7'b1100011), .eq(comparator_3_eq));  // open: gt, lt
  Comparator #(.width(7)) comparator_4 (.a(Instruction[6:0]), .b(7'b0000011), .eq(comparator_4_eq));  // open: gt, lt
  Comparator #(.width(7)) comparator_5 (.a(Instruction[6:0]), .b(7'b0100011), .eq(comparator_5_eq));  // open: gt, lt
  Comparator #(.width(7)) comparator_6 (.a(Instruction[6:0]), .b(7'b1101111), .eq(comparator_6_eq));  // open: gt, lt
  Comparator #(.width(7)) comparator_7 (.a(Instruction[6:0]), .b(7'b1100111), .eq(comparator_7_eq));  // open: gt, lt
  Comparator #(.width(7)) comparator_8 (.a(Instruction[6:0]), .b(7'b0010111), .eq(comparator_8_eq));  // open: gt, lt
  Comparator #(.width(7)) comparator_9 (.a(Instruction[6:0]), .b(7'b0110111), .eq(comparator_9_eq));  // open: gt, lt
  Multiplexer #(.select(3), .width(6)) multiplexer_6 (
    .in0(multiplexer_2_out), .in1(multiplexer_3_out), .in2(6'b000110), .in3(6'b000101), .in4(6'b000111),
    .in5(multiplexer_4_out), .in6(6'b001010), .in7(6'b001011), .out(RType), .sel(Instruction[14:12]));
  Multiplexer #(.select(3), .width(6)) multiplexer_7 (
    .in0(6'b000110), .in1(6'b000110), .in2(6'b000110), .in3(6'b000101), .in4(6'b000111), .in5(undriven),
    .in6(6'b001010), .in7(6'b001011), .out(BType), .sel(Instruction[14:12]));
  Priority_Encoder #(.select_enc(4)) priority_encoder_1 (
    .in0(comparator_1_eq), .in1(comparator_2_eq), .in2(comparator_3_eq), .in3(comparator_4_eq),
    .in4(comparator_5_eq), .in5(comparator_6_eq), .in6(comparator_7_eq), .in7(comparator_8_eq),
    .in8(comparator_9_eq), .out(PriOut), .en_in(1'b1));  // open: in9, in10, in11, in12, in13, in14, in15, gs, en_out
  Multiplexer #(.select(4), .width(6)) multiplexer_8 (
    .in0(IType), .in1(RType), .in2(BType), .in3(I2Type), .in4(SType), .in5(JType), .in6(I3Type), .in7(UType),
    .in8(U2Type), .out(ROMInput), .sel(PriOut));  // open: in9, in10, in11, in12, in13, in14, in15
  Comparator #(.width(4)) comparator_10 (.a(PriOut), .b(4'b0000), .eq(comparator_10_eq));  // open: gt, lt
  Comparator #(.width(4)) comparator_11 (.a(PriOut), .b(4'b0001));  // open: gt, eq, lt
  Comparator #(.width(4)) comparator_12 (.a(PriOut), .b(4'b0010));  // open: gt, eq, lt
  Comparator #(.width(4)) comparator_13 (.a(PriOut), .b(4'b0011));  // open: gt, eq, lt
  Comparator #(.width(4)) comparator_14 (.a(PriOut), .b(4'b0100));  // open: gt, eq, lt
  Comparator #(.width(4)) comparator_15 (.a(PriOut), .b(4'b0101));  // open: gt, eq, lt
  Comparator #(.width(4)) comparator_16 (.a(PriOut), .b(4'b0110));  // open: gt, eq, lt
  Comparator #(.width(4)) comparator_17 (.a(PriOut), .b(4'b0111));  // open: gt, eq, lt
  Comparator #(.width(4)) comparator_18 (.a(PriOut), .b(4'b1000));  // open: gt, eq, lt
  Multiplexer #(.enable("true"), .select(3), .width(3)) multiplexer_9 (
    .in0(3'b000), .in1(3'b001), .in2(3'b010), .in4(3'b100), .in5(3'b101), .in6(3'b110), .in7(3'b111),
    .out(multiplexer_9_out), .sel(Instruction[14:12]), .en(comparator_10_eq));  // open: in3
  Comparator #(.width(3)) comparator_19 (.a(multiplexer_9_out), .b(3'b101));  // open: gt, eq, lt

  // Other names for the same wires on the sheet: rd[4:0] = Instruction[11:7]; func3[2:0] = Instruction[14:12];
  //   rs1[4:0] = Instruction[19:15]; rs2[4:0] = Instruction[24:20]; func7[6:0] = Instruction[31:25]

  // Notes on the sheet:
  //   INPUTS to your circuit
  //   IType
  //   RType
  //   BType
  //   Connect ROM Input here ->
  //   I:0x13 = 001 0011，R:0x63=011 0011
  //   contents of rom_1 (hex, n*v repeats v):
  //   1001 1401 1601 1081 1481 1581 1101 1201 1281 1681 1301 1381 41 41 41 1041 10c1 1141 1241 12c1 16c1
  //   1341 13c1 842 842 842 4*64 74 74 1047 17c7 2069 2061 4*64 74 74 1047 17c7 2069 2061 2069 2061
  //   ROM FOR CONTROL LOGIC
  //   DON'T CHANGE THE LOCATIONS OF THE INPUTS AND OUTPUTS!
  //   This is only if you choose to do the ROM option
  //   CONNECT
  //   WIRE
  //   TO
  //   USE
  //   ROM
  //   OUTPUT from your circuit
  //   Reminder: If using ROM, use combinational logic for PCSel
endmodule
